# Fritzing sketch chickencoopV2 (saved by Fritzing 0.9.3b)

parts:
  M3 = DC Motor
  S3 = Pushbutton [package=THT]
  S4 = Pushbutton [package=THT]
  L298N1 = L298N DC motor driver
  MCU1 = Raspberry Pi Zero

nets:
  N1: M3.pin_1, L298N1.OUT4
  N2: M3.pin_2, L298N1.OUT3
  N3: S3.leg0, MCU1.pin_37
  N4: S3.leg1, S4.leg0, L298N1.GND, MCU1.pin_6, MCU1.pin_9, MCU1.pin_20, MCU1.pin_39
  N5: S4.leg1, MCU1.pin_18
  N6: L298N1.5V#7, MCU1.pin_2, MCU1.pin_4
  N7: L298N1.5V#9, L298N1.ENA
  N8: L298N1.5V#10, L298N1.ENB
  N9: L298N1.IN3, MCU1.pin_11
  N10: L298N1.IN4, MCU1.pin_13

custom parts:
  L298N DC motor driver: 2x DC motor driver with 78M05 positive voltage regulator (7..35 V) L298N: max 46 V, 2 A Set 5 V Enable jumper to enable 5 V regultor (needed for the L298N) and +5 V output at screw terminal or supply external +5 V at screw terminal Set ENA and/or ENB to +5 V to enable motor permanently or supply ENA and/or ENB with PWM signal IN1 and IN2 set rotation directory for motor A (OUT1/OUT2) IN2 and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
